# Fritzing sketch sketch (saved by Fritzing 0.9.4)
circuit board: 6.06853cm x 2.62824cm
breadboards: 1

parts:
  Q1 = Basic FET N-Channel [package="TO220 [THT]"]
  Q2 = Basic FET N-Channel [package="TO220 [THT]"]
  Q3 = Basic FET N-Channel [package="TO220 [THT]"]
  R1 = Resistor [tolerance=±5% resistance=15 package=THT]
  R2 = Resistor [tolerance=±5% resistance=15 package=THT]
  R3 = Resistor [tolerance=±5% resistance=15 package=THT]
  J1 = Screw terminal - 2 pins [package=THT]
  J2 = Screw terminal - 2 pins [package=THT]
  J3 = rounded female pin header, 4 pins [form="♀ (female rounded)"]
  Raspberry_Pi_1 = Raspberry Pi 3 [part_number=RPI-3-V1.2]

nets:
  N1: Q1.gate, R1.Pin_1
  N2: Q1.drain, J3.pin3
  N3: Q1.source, Q2.source, Q3.source, J1.pin2, Raspberry_Pi_1.GND
  N4: Q2.gate, R2.Pin_1
  N5: Q2.drain, J3.pin2
  N6: Q3.gate, R3.Pin_1
  N7: Q3.drain, J3.pin4
  N8: R1.Pin_0, Raspberry_Pi_1.GPIO17
  N9: R2.Pin_0, Raspberry_Pi_1.GPIO27
  N10: R3.Pin_0, Raspberry_Pi_1.GPIO22
  N11: J1.pin1, Raspberry_Pi_1.5V
  N12: J2.pin2, J3.pin1

notes:
  AGRB
  ATX
  Connector
  Breakout
  Lights, Raspberry Pi 12V RGB LED Strip Controller (Common Anode), 1
  x
  Rev 1
  Lights
  ATX Power Breakout
  5v   GND  12v
  LED Light Strip Connector
  --> A G R B
